# Fritzing sketch Candle (saved by Fritzing 1.0.1rc)
breadboards: 1

parts:
  Part1 = Adafruit HUZZAH32 ESP32 Feather [part_number="Adafruit #3405"]
  SERVO1 = Adafruit Feedback Servo (large)
  Part2 = 9-DOF Absolute Orientation IMU Fusion Breakout - BNO055
  Part3 = Lithium Ion Polymer Battery 3.7v 150mAh [part_number=1317]

nets:
  N1: Part1.IO16, SERVO1.Feedback
  N2: Part1.A5_IO4, SERVO1.Signal
  GND: Part1.GND, SERVO1.Ground, Part2.GND, Part3.negative
  N3: Part1.3.3V, Part2.5.0V
  N4: Part1.VBAT, SERVO1.Power, Part3.positive
  N5: Part1.SCL, Part2.SCL_5V
  N6: Part1.SDA, Part2.SDA_5V

custom parts:
  Adafruit Feedback Servo (large): Adafruit Feedback Servo (Small)
  9-DOF Absolute Orientation IMU Fusion Breakout - BNO055: A MEMS accelerometer, magnetometer and gyroscope on a single die with a high speed ARM Cortex-M0 based processor to digest all the sensor data, abstract the sensor fusion and real time requirements away, and spit out data you can use in quaternions, Euler angles or vectors.
  Lithium Ion Polymer Battery 3.7v 150mAh: Lithium ion polymer (also known as 'lipo' or 'lipoly') batteries are thin, light and powerful. The output ranges from 4.2V when completely charged to 3.7V. This battery has a capacity of 150mAh for a total of about 0.6 Wh. The batteries come pre-attached with a genuine 2-pin JST-PH connector as shown and include the necessary protection circuitry.
